// Logisim project hw4.circ as structural Verilog
module main (
  input  [2:0] in_1,
  input  reset
);

  wire ALU2_2_is_zero, and_1_out, and_2_out, and_3_out, clk, data_valid, is_addi, is_beq, is_bgt, is_gt,
       is_input, is_jal, is_output, load_mem_to_input, memory_latch_1_oe_latched, memory_latch_1_we_latched,
       MUX_data_vs_rs, MUX_j_vs_pc, not_1_out, not_sw, sei_or_rt, write_enable_RAM;
  wire [1:0] PC_ctrl;
  wire [2:0] alu_1_cmd, multiplexer_2_out, multiplexer_3_out, rd, rs, rt, shamt;
  wire [5:0] immed;
  wire [6:0] keyboard_1_data, tty_tunnel;
  wire [11:0] address;
  wire [15:0] ALU2_2_output, ALU2_output, bit_extender_1_out, keyboard_data, L,
       memory_latch_1_address_latched, memory_latch_1_data_in_latched, multiplexer_1_out, multiplexer_4_out,
       multiplexer_5_out, multiplexer_6_out, multiplexer_7_out, multiplexer_8_out, multiplexer_9_out,
       multiplexer_10_out, pc_counter_1_pcplus1, pc_output_reg, ra, ram_1_dout, registerfile_1_rs_2contents,
       rom_1_data;

  Multiplexer #(.select(2), .width(16), .enable("false")) multiplexer_1 (
    .in0(multiplexer_9_out), .in1(L), .in2(ra), .out(multiplexer_1_out), .sel(PC_ctrl));  // open: in3
  register pc (.in_1(multiplexer_1_out), .reset(reset), .clk(clk), .WE(clk), .output_reg(pc_output_reg));
  pc_extender pc_extender_1 (.in_1(address), .in_2(pc_output_reg), .L(L));
  pc_counter pc_counter_1 (.pc(pc_output_reg), .pcplus1(pc_counter_1_pcplus1));
  TTY #(.rows(13), .cols(80), .trigger("falling")) tty_1 (.data(tty_tunnel), .clk(clk), .we(is_output), .clr(reset));
  ROM #(.addrWidth(16), .dataWidth(16)) rom_1 (.addr(pc_output_reg), .data(rom_1_data));
  Clock clock_1 (.out(clk));
  Keyboard #(.trigger("falling")) keyboard_1 (
    .clk(clk), .re(is_input), .clr(reset), .avail(data_valid), .data(keyboard_1_data));
  keyboard_wrapper keyboard_wrapper_1 (.in_1(keyboard_1_data), .is_valid(data_valid), .out_3(keyboard_data));
  Multiplexer #(.width(3), .enable("false")) multiplexer_2 (
    .in0(rd), .in1(3'b111), .out(multiplexer_2_out), .sel(is_jal));
  combinatorial_logic combinatorial_logic_1 (
    .in_1(rom_1_data), .rs(rs), .rt(rt), .rd(rd), .shamt(shamt), .immed(immed), .address(address),
    .alu1_chooser(alu_1_cmd), .not_sw(not_sw), .is_output(is_output), .is_bgt(is_bgt), .is_beq(is_beq),
    .sei_or_rt(sei_or_rt), .is_addi(is_addi), .write_enable_RAM(write_enable_RAM),
    .load_mem_to_input(load_mem_to_input), .MUX_data_vs_rs(MUX_data_vs_rs), .MUX_j_vs_pc(MUX_j_vs_pc),
    .is_input(is_input), .PC_ctrl(PC_ctrl), .is_jal(is_jal));
  Multiplexer #(.width(3), .enable("false")) multiplexer_3 (
    .in0(multiplexer_2_out), .in1(rt), .out(multiplexer_3_out), .sel(is_addi));
  Multiplexer #(.width(16), .enable("false")) multiplexer_4 (
    .in0(multiplexer_5_out), .in1(pc_counter_1_pcplus1), .out(multiplexer_4_out), .sel(is_jal));
  RegisterFile registerfile_1 (
    .sw(not_sw), .rd(multiplexer_3_out), .clk(clk), .reset(reset), .data_in(multiplexer_4_out), .rs2(rt),
    .rs1(rs), .rs_1_contents(ra), .rs_2contents(registerfile_1_rs_2contents));
  assign bit_extender_1_out = {{10{immed[5]}}, immed};  // Bit_Extender bit_extender_1
  Multiplexer #(.width(16), .enable("false")) multiplexer_5 (
    .in0(multiplexer_10_out), .in1(keyboard_data), .out(multiplexer_5_out), .sel(is_input));
  Multiplexer #(.width(16), .enable("false")) multiplexer_6 (
    .in0(registerfile_1_rs_2contents), .in1(bit_extender_1_out), .out(multiplexer_6_out), .sel(sei_or_rt));
  ALU ALU2 (
    .in1(pc_counter_1_pcplus1), .in2(bit_extender_1_out), .bitshift(in_1), .\output (ALU2_output));  // open: in_4, is_zero, is_gt
  not not_1 (not_1_out, ALU2_2_is_zero);
  ALU ALU2_2 (
    .in1(ra), .in2(multiplexer_6_out), .bitshift(shamt), .in_4(alu_1_cmd), .\output (ALU2_2_output),
    .is_zero(ALU2_2_is_zero), .is_gt(is_gt));
  and and_1 (and_1_out, is_beq, not_1_out);
  memory_latch memory_latch_1 (
    .address(ALU2_2_output), .WE(write_enable_RAM), .clk(clk), .data_in(registerfile_1_rs_2contents),
    .address_latched(memory_latch_1_address_latched), .WE_latched(memory_latch_1_we_latched),
    .OE_latched(memory_latch_1_oe_latched), .data_in_latched(memory_latch_1_data_in_latched));
  Multiplexer #(.width(16), .enable("false")) multiplexer_7 (
    .in0(pc_counter_1_pcplus1), .in1(ALU2_output), .out(multiplexer_7_out), .sel(and_1_out));
  RAM #(.addrWidth(16), .dataWidth(16), .trigger("high"), .databus("bibus")) ram_1 (
    .addr(memory_latch_1_address_latched), .we(memory_latch_1_we_latched), .oe(memory_latch_1_oe_latched),
    .din(memory_latch_1_data_in_latched), .dout(ram_1_dout));
  Multiplexer #(.width(16), .enable("false")) multiplexer_8 (
    .in0(multiplexer_7_out), .in1(ALU2_output), .out(multiplexer_8_out), .sel(and_3_out));
  and and_2 (and_2_out, is_bgt, ALU2_2_is_zero);
  TTY_wrapper tty_wrapper_1 (.in_1(ra), .out_2(tty_tunnel));
  Multiplexer #(.width(16), .enable("false")) multiplexer_9 (
    .in0(multiplexer_8_out), .in1(bit_extender_1_out), .out(multiplexer_9_out), .sel(MUX_j_vs_pc));
  and and_3 (and_3_out, is_gt, and_2_out);
  Multiplexer #(.width(16), .enable("false")) multiplexer_10 (
    .in0(ALU2_2_output), .in1(ram_1_dout), .out(multiplexer_10_out), .sel(MUX_data_vs_rs));

  // Notes on the sheet:
  //   contents of rom_1 (hex, n*v repeats v):
  //   80c0 804f 8090 5441 403f e009 4206 d00f 9488 8272 fe00 8441 403f 8441 403f 403f
endmodule

module memory_latch (
  input  [15:0] address,
  input  WE,
  input  clk,
  input  [15:0] data_in,
  output [15:0] address_latched,
  output WE_latched,
  output OE_latched,
  output [15:0] data_in_latched
);

  wire d_ff_1_q;
  wire [15:0] register_1_q;

  Register #(.width(16), .trigger("falling")) register_1 (
    .D(address), .en(WE), .clk(clk), .Q(register_1_q));  // open: clr
  D_Flip_Flop #(.trigger("falling")) d_ff_1 (.D(WE), .clk(clk), .Q(d_ff_1_q));  // open: Qn, preset, reset
  Register #(.width(16), .trigger("falling")) register_2 (
    .D(data_in), .en(WE), .clk(clk), .Q(data_in_latched));  // open: clr
  Multiplexer #(.width(16), .enable("false")) multiplexer_1 (
    .in0(address), .in1(register_1_q), .out(address_latched), .sel(d_ff_1_q));
  and and_1 (WE_latched, clk, d_ff_1_q);
  not not_1 (OE_latched, WE_latched);
endmodule

module register (
  input  [15:0] in_1,
  input  reset,
  input  clk,
  input  WE,
  output [15:0] output_reg
);

  wire tock;

  and and_1 (tock, clk, WE);
  D_Flip_Flop d_ff_1 (.D(in_1[0]), .clk(tock), .Q(output_reg[0]), .reset(reset));  // open: Qn, preset
  D_Flip_Flop d_ff_2 (.D(in_1[2]), .clk(tock), .Q(output_reg[2]), .reset(reset));  // open: Qn, preset
  D_Flip_Flop d_ff_3 (.D(in_1[4]), .clk(tock), .Q(output_reg[4]), .reset(reset));  // open: Qn, preset
  D_Flip_Flop d_ff_4 (.D(in_1[6]), .clk(tock), .Q(output_reg[6]), .reset(reset));  // open: Qn, preset
  D_Flip_Flop d_ff_5 (.D(in_1[8]), .clk(tock), .Q(output_reg[8]), .reset(reset));  // open: Qn, preset
  D_Flip_Flop d_ff_6 (.D(in_1[10]), .clk(tock), .Q(output_reg[10]), .reset(reset));  // open: Qn, preset
  D_Flip_Flop d_ff_7 (.D(in_1[12]), .clk(tock), .Q(output_reg[12]), .reset(reset));  // open: Qn, preset
  D_Flip_Flop d_ff_8 (.D(in_1[14]), .clk(tock), .Q(output_reg[14]), .reset(reset));  // open: Qn, preset
  D_Flip_Flop d_ff_9 (.D(in_1[1]), .clk(tock), .Q(output_reg[1]), .reset(reset));  // open: Qn, preset
  D_Flip_Flop d_ff_10 (.D(in_1[3]), .clk(tock), .Q(output_reg[3]), .reset(reset));  // open: Qn, preset
  D_Flip_Flop d_ff_11 (.D(in_1[5]), .clk(tock), .Q(output_reg[5]), .reset(reset));  // open: Qn, preset
  D_Flip_Flop d_ff_12 (.D(in_1[7]), .clk(tock), .Q(output_reg[7]), .reset(reset));  // open: Qn, preset
  D_Flip_Flop d_ff_13 (.D(in_1[9]), .clk(tock), .Q(output_reg[9]), .reset(reset));  // open: Qn, preset
  D_Flip_Flop d_ff_14 (.D(in_1[11]), .clk(tock), .Q(output_reg[11]), .reset(reset));  // open: Qn, preset
  D_Flip_Flop d_ff_15 (.D(in_1[13]), .clk(tock), .Q(output_reg[13]), .reset(reset));  // open: Qn, preset
  D_Flip_Flop d_ff_16 (.D(in_1[15]), .clk(tock), .Q(output_reg[15]), .reset(reset));  // open: Qn, preset

  // Other names for the same wires on the sheet: R = reset
endmodule

module RegisterFile (
  input  sw,
  input  [2:0] rd,
  input  clk,
  input  [2:0] rs1,
  input  reset,
  input  [15:0] data_in,
  input  [2:0] rs2,
  output [15:0] rs_1_contents,
  output [15:0] rs_2contents
);

  wire decoder_1_out0, decoder_1_out1, decoder_1_out2, decoder_1_out3, decoder_1_out4, decoder_1_out5,
       decoder_1_out6, decoder_1_out7, not_1_out;
  wire [15:0] register_1_p5, register_2_output_reg, register_3_output_reg, register_4_output_reg,
       register_5_output_reg, register_6_output_reg, register_7_output_reg, register_8_output_reg;

  Decoder #(.select(3)) decoder_1 (
    .out0(decoder_1_out0), .out1(decoder_1_out1), .out2(decoder_1_out2), .out3(decoder_1_out3),
    .out4(decoder_1_out4), .out5(decoder_1_out5), .out6(decoder_1_out6), .out7(decoder_1_out7), .sel(rd),
    .en(sw));
  not not_1 (not_1_out, clk);
  // register register_1: pin names not known; wires that end beside it: decoder_1_out0, data_in, reset, not_1_out, register_1_p5
  register register_2 (
    .in_1(data_in), .reset(reset), .clk(not_1_out), .WE(decoder_1_out1), .output_reg(register_2_output_reg));
  register register_3 (
    .in_1(data_in), .reset(reset), .clk(not_1_out), .WE(decoder_1_out2), .output_reg(register_3_output_reg));
  register register_4 (
    .in_1(data_in), .reset(reset), .clk(not_1_out), .WE(decoder_1_out3), .output_reg(register_4_output_reg));
  register register_5 (
    .in_1(data_in), .reset(reset), .clk(not_1_out), .WE(decoder_1_out4), .output_reg(register_5_output_reg));
  register register_6 (
    .in_1(data_in), .reset(reset), .clk(not_1_out), .WE(decoder_1_out5), .output_reg(register_6_output_reg));
  register register_7 (
    .in_1(data_in), .reset(reset), .clk(not_1_out), .WE(decoder_1_out6), .output_reg(register_7_output_reg));
  register register_8 (
    .in_1(data_in), .reset(reset), .clk(not_1_out), .WE(decoder_1_out7), .output_reg(register_8_output_reg));
  // Probe on register_8_output_reg
  // Probe on register_1_p5
  // Probe on register_3_output_reg
  // Probe on register_4_output_reg
  // Probe on register_6_output_reg
  // Probe on register_7_output_reg
  // Probe on register_2_output_reg
  // Probe on register_5_output_reg
  Multiplexer #(.select(3), .width(16), .enable("false")) multiplexer_1 (
    .in0(register_1_p5), .in1(register_2_output_reg), .in2(register_3_output_reg),
    .in3(register_4_output_reg), .in4(register_5_output_reg), .in5(register_6_output_reg),
    .in6(register_7_output_reg), .in7(register_8_output_reg), .out(rs_2contents), .sel(rs2));
  Multiplexer #(.select(3), .width(16), .enable("false")) multiplexer_2 (
    .in0(register_1_p5), .in1(register_2_output_reg), .in2(register_3_output_reg),
    .in3(register_4_output_reg), .in4(register_5_output_reg), .in5(register_6_output_reg),
    .in6(register_7_output_reg), .in7(register_8_output_reg), .out(rs_1_contents), .sel(rs1));
endmodule

module ALU (
  input  [15:0] in1,
  input  [15:0] in2,
  input  [2:0] bitshift,
  input  [2:0] in_4,
  output [15:0] \output ,
  output is_zero,
  output is_gt
);

  wire [15:0] adder_1_result, adder_2_result, and_1_out, arithmetic_shift_1_out_3,
       barrel_shifter_left_1_rs_out, or_1_out;

  adder adder_1 (.A(in1), .B(in2), .result(adder_1_result));  // open: in_1, ovf
  adder adder_2 (.in_1(1'b1), .A(in1), .B(in2), .result(adder_2_result));  // open: ovf
  assign and_1_out = in1 & in2;  // AND_Gate and_1, 16 bits wide
  barrel_shifter_left barrel_shifter_left_1 (.rs_in(in1), .bitshift(bitshift), .rs_out(barrel_shifter_left_1_rs_out));
  arithmetic_shift arithmetic_shift_1 (.in_1(in1), .in_2(bitshift), .out_3(arithmetic_shift_1_out_3));
  assign or_1_out = in1 | in2;  // OR_Gate or_1, 16 bits wide
  Multiplexer #(.select(3), .width(16), .enable("false")) multiplexer_1 (
    .in0(adder_1_result), .in1(adder_2_result), .in2(and_1_out), .in3(barrel_shifter_left_1_rs_out),
    .in4(arithmetic_shift_1_out_3), .in5(or_1_out), .out(\output ), .sel(in_4));  // open: in6, in7
  or or_2 (is_zero, \output [0], \output [1], \output [2], \output [3], \output [4], \output [5], \output [6], \output [7], \output [8], \output [9], \output [10], \output [11], \output [12], \output [13], \output [14], \output [15]);
  not not_1 (is_gt, \output [15]);

  // Notes on the sheet:
  //   Outputs:
  //   Inputs:
  //   is_zero: 0 if is zero, 1 if isn't
  //   output= modified register
  //   in1: rs1
  //   in2: rs2
  //   bitshift= shamt
  //   mux select bit
  //   Mux Select Options:
  //   000: add
  //   001: subtract
  //   010: and
  //   011: shift left
  //   101: or
  //   100: arithmetic shift right
endmodule

module adder (
  input  in_1,
  input  [15:0] A,
  input  [15:0] B,
  output [15:0] result,
  output ovf
);

  wire and_1_out, and_2_out, and_3_out, and_4_out, and_5_out, and_6_out, and_7_out, and_8_out, and_9_out,
       and_10_out, and_11_out, and_12_out, and_13_out, and_14_out, and_15_out, and_16_out, and_17_out,
       and_18_out, and_19_out, and_20_out, and_21_out, and_22_out, and_23_out, and_24_out, and_25_out,
       and_26_out, and_27_out, and_28_out, and_29_out, and_30_out, and_31_out, and_32_out, and_33_out,
       and_34_out, and_35_out, and_36_out, and_37_out, and_38_out, and_39_out, and_40_out, and_41_out,
       and_42_out, and_43_out, and_44_out, and_45_out, and_46_out, and_47_out, and_48_out, and_49_out,
       and_50_out, and_51_out, and_52_out, and_53_out, and_54_out, and_55_out, and_56_out, and_57_out,
       and_58_out, and_59_out, and_60_out, and_61_out, and_62_out, and_63_out, and_64_out, and_65_out,
       and_66_out, and_67_out, and_68_out, and_69_out, and_70_out, and_71_out, and_72_out, and_73_out,
       and_74_out, and_75_out, and_76_out, and_77_out, and_78_out, and_79_out, and_80_out, and_81_out,
       and_82_out, and_83_out, and_84_out, not_1_out, not_2_out, not_3_out, not_4_out, not_5_out, not_6_out,
       not_7_out, not_8_out, not_9_out, not_10_out, not_11_out, not_12_out, not_13_out, not_14_out,
       not_15_out, not_16_out, not_17_out, not_18_out, not_19_out, not_20_out, not_21_out, not_22_out,
       not_23_out, not_24_out, not_25_out, not_26_out, not_27_out, not_28_out, not_29_out, not_30_out,
       not_31_out, not_32_out, not_33_out, not_34_out, not_35_out, not_36_out, not_37_out, not_38_out,
       not_39_out, not_40_out, not_41_out, not_42_out, not_43_out, not_44_out, not_45_out, not_46_out,
       not_47_out, not_48_out, not_49_out, not_50_out, not_51_out, or_7_out, or_8_out, or_9_out, or_10_out,
       or_11_out, or_12_out, or_19_out, or_20_out, or_21_out, or_22_out, or_23_out, or_24_out, or_29_out,
       or_30_out, or_31_out, xor_1_out, xor_2_out, xor_3_out, xor_4_out, xor_5_out, xor_6_out, xor_7_out,
       xor_8_out, xor_9_out, xor_10_out, xor_11_out, xor_12_out, xor_13_out, xor_14_out, xor_15_out,
       xor_16_out, xor_17_out, xor_18_out, xor_19_out, xor_20_out, xor_21_out, xor_22_out, xor_23_out,
       xor_24_out, xor_25_out, xor_26_out, xor_27_out, xor_28_out, xor_29_out, xor_30_out, xor_31_out,
       xor_32_out, xor_33_out, xor_34_out, xor_35_out, xor_36_out, xor_37_out, xor_38_out, xor_39_out,
       xor_40_out, xor_41_out, xor_42_out, xor_43_out, xor_44_out, xor_45_out, xor_46_out, xor_47_out,
       xor_48_out;

  xor xor_1 (xor_1_out, B[0], in_1);
  xor xor_2 (xor_2_out, B[1], in_1);
  xor xor_3 (xor_3_out, B[2], in_1);
  xor xor_4 (xor_4_out, B[3], in_1);
  xor xor_5 (xor_5_out, B[4], in_1);
  xor xor_6 (xor_6_out, B[5], in_1);
  not not_1 (not_1_out, A[0]);
  not not_2 (not_2_out, xor_1_out);
  not not_3 (not_3_out, A[1]);
  not not_4 (not_4_out, xor_2_out);
  not not_5 (not_5_out, A[2]);
  not not_6 (not_6_out, xor_3_out);
  xor xor_7 (xor_7_out, A[0], xor_1_out);
  not not_7 (not_7_out, in_1);
  and and_1 (and_1_out, not_1_out, in_1, not_2_out);
  xor xor_8 (xor_8_out, A[1], xor_2_out);
  not not_8 (not_8_out, or_7_out);
  and and_2 (and_2_out, not_3_out, or_7_out, not_4_out);
  xor xor_9 (xor_9_out, A[2], xor_3_out);
  and and_3 (and_3_out, not_5_out, or_8_out, not_6_out);
  xor xor_10 (xor_10_out, A[3], xor_4_out);
  not not_9 (not_9_out, A[3]);
  and and_4 (and_4_out, not_9_out, or_9_out, not_10_out);
  not not_10 (not_10_out, xor_4_out);
  xor xor_11 (xor_11_out, A[4], xor_5_out);
  not not_11 (not_11_out, A[4]);
  not not_12 (not_12_out, xor_5_out);
  xor xor_12 (xor_12_out, A[5], xor_6_out);
  not not_13 (not_13_out, A[5]);
  not not_14 (not_14_out, xor_6_out);
  and and_5 (and_5_out, xor_7_out, not_7_out);
  and and_6 (and_6_out, A[0], xor_1_out, in_1);
  and and_7 (and_7_out, A[0], xor_1_out);
  and and_8 (and_8_out, xor_8_out, not_8_out);
  and and_9 (and_9_out, A[1], xor_2_out, or_7_out);
  and and_10 (and_10_out, A[1], xor_2_out);
  and and_11 (and_11_out, xor_9_out, not_15_out);
  not not_15 (not_15_out, or_8_out);
  and and_12 (and_12_out, A[2], xor_3_out, or_8_out);
  and and_13 (and_13_out, A[2], xor_3_out);
  not not_16 (not_16_out, or_9_out);
  and and_14 (and_14_out, A[3], xor_4_out, or_9_out);
  and and_15 (and_15_out, A[3], xor_4_out);
  not not_17 (not_17_out, or_10_out);
  and and_16 (and_16_out, A[4], xor_5_out, or_10_out);
  and and_17 (and_17_out, not_11_out, or_10_out, not_12_out);
  not not_18 (not_18_out, or_11_out);
  and and_18 (and_18_out, A[5], xor_6_out, or_11_out);
  and and_19 (and_19_out, not_13_out, or_11_out, not_14_out);
  xor xor_13 (xor_13_out, A[0], xor_1_out);
  xor xor_14 (xor_14_out, A[1], xor_2_out);
  and and_20 (and_20_out, xor_10_out, not_16_out);
  and and_21 (and_21_out, xor_11_out, not_17_out);
  and and_22 (and_22_out, A[4], xor_5_out);
  and and_23 (and_23_out, xor_12_out, not_18_out);
  and and_24 (and_24_out, A[5], xor_6_out);
  or or_1 (result[0], and_5_out, and_1_out, and_6_out);
  and and_25 (and_25_out, in_1, xor_13_out);
  or or_2 (result[1], and_8_out, and_2_out, and_9_out);
  and and_26 (and_26_out, or_7_out, xor_14_out);
  or or_3 (result[2], and_11_out, and_3_out, and_12_out);
  and and_27 (and_27_out, or_8_out, xor_15_out);
  xor xor_15 (xor_15_out, A[2], xor_3_out);
  or or_4 (result[3], and_20_out, and_4_out, and_14_out);
  xor xor_16 (xor_16_out, A[3], xor_4_out);
  or or_5 (result[4], and_21_out, and_17_out, and_16_out);
  xor xor_17 (xor_17_out, A[4], xor_5_out);
  or or_6 (result[5], and_23_out, and_19_out, and_18_out);
  xor xor_18 (xor_18_out, A[5], xor_6_out);
  or or_7 (or_7_out, and_7_out, and_25_out);
  or or_8 (or_8_out, and_10_out, and_26_out);
  or or_9 (or_9_out, and_13_out, and_27_out);
  and and_28 (and_28_out, or_9_out, xor_16_out);
  and and_29 (and_29_out, or_10_out, xor_17_out);
  and and_30 (and_30_out, or_11_out, xor_18_out);
  or or_10 (or_10_out, and_15_out, and_28_out);
  or or_11 (or_11_out, and_22_out, and_29_out);
  or or_12 (or_12_out, and_24_out, and_30_out);
  xor xor_19 (xor_19_out, B[6], in_1);
  xor xor_20 (xor_20_out, B[7], in_1);
  xor xor_21 (xor_21_out, B[8], in_1);
  xor xor_22 (xor_22_out, B[9], in_1);
  xor xor_23 (xor_23_out, B[10], in_1);
  xor xor_24 (xor_24_out, B[11], in_1);
  not not_19 (not_19_out, A[9]);
  not not_20 (not_20_out, xor_22_out);
  xor xor_25 (xor_25_out, A[6], xor_19_out);
  not not_21 (not_21_out, A[6]);
  and and_31 (and_31_out, not_21_out, or_12_out, not_22_out);
  not not_22 (not_22_out, xor_19_out);
  xor xor_26 (xor_26_out, A[7], xor_20_out);
  not not_23 (not_23_out, A[7]);
  not not_24 (not_24_out, xor_20_out);
  not not_25 (not_25_out, A[8]);
  not not_26 (not_26_out, xor_21_out);
  xor xor_27 (xor_27_out, A[9], xor_22_out);
  and and_32 (and_32_out, not_19_out, or_22_out, not_20_out);
  xor xor_28 (xor_28_out, A[10], xor_23_out);
  not not_27 (not_27_out, A[10]);
  and and_33 (and_33_out, not_27_out, or_19_out, not_28_out);
  not not_28 (not_28_out, xor_23_out);
  xor xor_29 (xor_29_out, A[11], xor_24_out);
  not not_29 (not_29_out, A[11]);
  and and_34 (and_34_out, not_29_out, or_23_out, not_30_out);
  not not_30 (not_30_out, xor_24_out);
  not not_31 (not_31_out, or_12_out);
  and and_35 (and_35_out, A[6], xor_19_out, or_12_out);
  and and_36 (and_36_out, A[6], xor_19_out);
  not not_32 (not_32_out, or_20_out);
  and and_37 (and_37_out, A[7], xor_20_out, or_20_out);
  and and_38 (and_38_out, not_23_out, or_20_out, not_24_out);
  xor xor_30 (xor_30_out, A[8], xor_21_out);
  not not_33 (not_33_out, or_21_out);
  and and_39 (and_39_out, A[8], xor_21_out, or_21_out);
  and and_40 (and_40_out, not_25_out, or_21_out, not_26_out);
  and and_41 (and_41_out, xor_27_out, not_34_out);
  not not_34 (not_34_out, or_22_out);
  and and_42 (and_42_out, A[9], xor_22_out, or_22_out);
  and and_43 (and_43_out, A[9], xor_22_out);
  not not_35 (not_35_out, or_19_out);
  and and_44 (and_44_out, A[10], xor_23_out, or_19_out);
  and and_45 (and_45_out, A[10], xor_23_out);
  not not_36 (not_36_out, or_23_out);
  and and_46 (and_46_out, A[11], xor_24_out, or_23_out);
  and and_47 (and_47_out, A[11], xor_24_out);
  and and_48 (and_48_out, xor_25_out, not_31_out);
  and and_49 (and_49_out, xor_26_out, not_32_out);
  and and_50 (and_50_out, A[7], xor_20_out);
  and and_51 (and_51_out, xor_30_out, not_33_out);
  and and_52 (and_52_out, A[8], xor_21_out);
  and and_53 (and_53_out, xor_28_out, not_35_out);
  and and_54 (and_54_out, xor_29_out, not_36_out);
  or or_13 (result[6], and_48_out, and_31_out, and_35_out);
  xor xor_31 (xor_31_out, A[6], xor_19_out);
  or or_14 (result[7], and_49_out, and_38_out, and_37_out);
  xor xor_32 (xor_32_out, A[7], xor_20_out);
  or or_15 (result[8], and_51_out, and_40_out, and_39_out);
  xor xor_33 (xor_33_out, A[8], xor_21_out);
  or or_16 (result[9], and_41_out, and_32_out, and_42_out);
  and and_55 (and_55_out, or_22_out, xor_34_out);
  xor xor_34 (xor_34_out, A[9], xor_22_out);
  or or_17 (result[10], and_53_out, and_33_out, and_44_out);
  xor xor_35 (xor_35_out, A[10], xor_23_out);
  or or_18 (result[11], and_54_out, and_34_out, and_46_out);
  xor xor_36 (xor_36_out, A[11], xor_24_out);
  and and_56 (and_56_out, or_12_out, xor_31_out);
  and and_57 (and_57_out, or_20_out, xor_32_out);
  and and_58 (and_58_out, or_21_out, xor_33_out);
  or or_19 (or_19_out, and_43_out, and_55_out);
  and and_59 (and_59_out, or_19_out, xor_35_out);
  and and_60 (and_60_out, or_23_out, xor_36_out);
  or or_20 (or_20_out, and_36_out, and_56_out);
  or or_21 (or_21_out, and_50_out, and_57_out);
  or or_22 (or_22_out, and_52_out, and_58_out);
  or or_23 (or_23_out, and_45_out, and_59_out);
  or or_24 (or_24_out, and_47_out, and_60_out);
  xor xor_37 (xor_37_out, B[12], in_1);
  xor xor_38 (xor_38_out, B[13], in_1);
  xor xor_39 (xor_39_out, B[14], in_1);
  xor xor_40 (xor_40_out, B[15], in_1);
  not not_37 (not_37_out, A[12]);
  not not_38 (not_38_out, xor_37_out);
  not not_39 (not_39_out, A[13]);
  not not_40 (not_40_out, xor_38_out);
  not not_41 (not_41_out, A[14]);
  not not_42 (not_42_out, xor_39_out);
  not not_43 (not_43_out, A[15]);
  not not_44 (not_44_out, xor_40_out);
  xor xor_41 (xor_41_out, A[12], xor_37_out);
  not not_45 (not_45_out, or_24_out);
  and and_61 (and_61_out, not_37_out, or_24_out, not_38_out);
  xor xor_42 (xor_42_out, A[13], xor_38_out);
  not not_46 (not_46_out, or_29_out);
  and and_62 (and_62_out, not_39_out, or_29_out, not_40_out);
  xor xor_43 (xor_43_out, A[14], xor_39_out);
  not not_47 (not_47_out, or_30_out);
  and and_63 (and_63_out, not_41_out, or_30_out, not_42_out);
  xor xor_44 (xor_44_out, A[15], xor_40_out);
  not not_48 (not_48_out, or_31_out);
  and and_64 (and_64_out, not_43_out, or_31_out, not_44_out);
  and and_65 (and_65_out, xor_41_out, not_45_out);
  and and_66 (and_66_out, A[12], xor_37_out, or_24_out);
  and and_67 (and_67_out, A[12], xor_37_out);
  and and_68 (and_68_out, xor_42_out, not_46_out);
  and and_69 (and_69_out, A[13], xor_38_out, or_29_out);
  and and_70 (and_70_out, A[13], xor_38_out);
  and and_71 (and_71_out, xor_43_out, not_47_out);
  and and_72 (and_72_out, A[14], xor_39_out, or_30_out);
  and and_73 (and_73_out, A[14], xor_39_out);
  and and_74 (and_74_out, xor_44_out, not_48_out);
  and and_75 (and_75_out, A[15], xor_40_out, or_31_out);
  and and_76 (and_76_out, A[15], xor_40_out);
  xor xor_45 (xor_45_out, A[12], xor_37_out);
  xor xor_46 (xor_46_out, A[13], xor_38_out);
  xor xor_47 (xor_47_out, A[14], xor_39_out);
  xor xor_48 (xor_48_out, A[15], xor_40_out);
  or or_25 (result[12], and_65_out, and_61_out, and_66_out);
  and and_77 (and_77_out, or_24_out, xor_45_out);
  or or_26 (result[13], and_68_out, and_62_out, and_69_out);
  and and_78 (and_78_out, or_29_out, xor_46_out);
  or or_27 (result[14], and_71_out, and_63_out, and_72_out);
  and and_79 (and_79_out, or_30_out, xor_47_out);
  or or_28 (result[15], and_74_out, and_64_out, and_75_out);
  and and_80 (and_80_out, or_31_out, xor_48_out);
  or or_29 (or_29_out, and_67_out, and_77_out);
  or or_30 (or_30_out, and_70_out, and_78_out);
  or or_31 (or_31_out, and_73_out, and_79_out);
  // OR_Gate or_32 has open pins: in0=and_76_out, in1=and_80_out, out=open
  not not_49 (not_49_out, xor_40_out);
  not not_50 (not_50_out, A[15]);
  and and_81 (and_81_out, not_49_out, not_50_out);
  not not_51 (not_51_out, result[15]);
  and and_82 (and_82_out, xor_40_out, A[15]);
  or or_33 (ovf, and_83_out, and_84_out);
  and and_83 (and_83_out, not_51_out, and_82_out);
  and and_84 (and_84_out, result[15], and_81_out);
endmodule

module bit_shifter_left (
  input  in_1,
  input  [15:0] rs_a,
  input  y_n,
  output [15:0] shifted_rs
);

  Multiplexer #(.enable("false")) multiplexer_1 (.in0(rs_a[0]), .in1(in_1), .out(shifted_rs[0]), .sel(y_n));
  Multiplexer #(.enable("false")) multiplexer_2 (.in0(rs_a[1]), .in1(rs_a[0]), .out(shifted_rs[1]), .sel(y_n));
  Multiplexer #(.enable("false")) multiplexer_3 (.in0(rs_a[2]), .in1(rs_a[1]), .out(shifted_rs[2]), .sel(y_n));
  Multiplexer #(.enable("false")) multiplexer_4 (.in0(rs_a[3]), .in1(rs_a[2]), .out(shifted_rs[3]), .sel(y_n));
  Multiplexer #(.enable("false")) multiplexer_5 (.in0(rs_a[4]), .in1(rs_a[3]), .out(shifted_rs[4]), .sel(y_n));
  Multiplexer #(.enable("false")) multiplexer_6 (.in0(rs_a[5]), .in1(rs_a[4]), .out(shifted_rs[5]), .sel(y_n));
  Multiplexer #(.enable("false")) multiplexer_7 (.in0(rs_a[6]), .in1(rs_a[5]), .out(shifted_rs[6]), .sel(y_n));
  Multiplexer #(.enable("false")) multiplexer_8 (.in0(rs_a[7]), .in1(rs_a[6]), .out(shifted_rs[7]), .sel(y_n));
  Multiplexer #(.enable("false")) multiplexer_9 (.in0(rs_a[8]), .in1(rs_a[7]), .out(shifted_rs[8]), .sel(y_n));
  Multiplexer #(.enable("false")) multiplexer_10 (.in0(rs_a[9]), .in1(rs_a[8]), .out(shifted_rs[9]), .sel(y_n));
  Multiplexer #(.enable("false")) multiplexer_11 (.in0(rs_a[10]), .in1(rs_a[9]), .out(shifted_rs[10]), .sel(y_n));
  Multiplexer #(.enable("false")) multiplexer_12 (.in0(rs_a[11]), .in1(rs_a[10]), .out(shifted_rs[11]), .sel(y_n));
  Multiplexer #(.enable("false")) multiplexer_13 (.in0(rs_a[12]), .in1(rs_a[11]), .out(shifted_rs[12]), .sel(y_n));
  Multiplexer #(.enable("false")) multiplexer_14 (.in0(rs_a[13]), .in1(rs_a[12]), .out(shifted_rs[13]), .sel(y_n));
  Multiplexer #(.enable("false")) multiplexer_15 (.in0(rs_a[14]), .in1(rs_a[13]), .out(shifted_rs[14]), .sel(y_n));
  Multiplexer #(.enable("false")) multiplexer_16 (.in0(rs_a[15]), .in1(rs_a[14]), .out(shifted_rs[15]), .sel(y_n));
endmodule

module bit_shift_left_2 (
  input  in_1,
  input  [15:0] rs_a,
  input  y_n,
  output [15:0] shifted_rs
);

  Multiplexer #(.enable("false")) multiplexer_1 (.in0(rs_a[0]), .in1(in_1), .out(shifted_rs[0]), .sel(y_n));
  Multiplexer #(.enable("false")) multiplexer_2 (.in0(rs_a[1]), .in1(in_1), .out(shifted_rs[1]), .sel(y_n));
  Multiplexer #(.enable("false")) multiplexer_3 (.in0(rs_a[2]), .in1(rs_a[0]), .out(shifted_rs[2]), .sel(y_n));
  Multiplexer #(.enable("false")) multiplexer_4 (.in0(rs_a[3]), .in1(rs_a[1]), .out(shifted_rs[3]), .sel(y_n));
  Multiplexer #(.enable("false")) multiplexer_5 (.in0(rs_a[4]), .in1(rs_a[2]), .out(shifted_rs[4]), .sel(y_n));
  Multiplexer #(.enable("false")) multiplexer_6 (.in0(rs_a[5]), .in1(rs_a[3]), .out(shifted_rs[5]), .sel(y_n));
  Multiplexer #(.enable("false")) multiplexer_7 (.in0(rs_a[6]), .in1(rs_a[4]), .out(shifted_rs[6]), .sel(y_n));
  Multiplexer #(.enable("false")) multiplexer_8 (.in0(rs_a[7]), .in1(rs_a[5]), .out(shifted_rs[7]), .sel(y_n));
  Multiplexer #(.enable("false")) multiplexer_9 (.in0(rs_a[8]), .in1(rs_a[6]), .out(shifted_rs[8]), .sel(y_n));
  Multiplexer #(.enable("false")) multiplexer_10 (.in0(rs_a[9]), .in1(rs_a[7]), .out(shifted_rs[9]), .sel(y_n));
  Multiplexer #(.enable("false")) multiplexer_11 (.in0(rs_a[10]), .in1(rs_a[8]), .out(shifted_rs[10]), .sel(y_n));
  Multiplexer #(.enable("false")) multiplexer_12 (.in0(rs_a[11]), .in1(rs_a[9]), .out(shifted_rs[11]), .sel(y_n));
  Multiplexer #(.enable("false")) multiplexer_13 (.in0(rs_a[12]), .in1(rs_a[10]), .out(shifted_rs[12]), .sel(y_n));
  Multiplexer #(.enable("false")) multiplexer_14 (.in0(rs_a[13]), .in1(rs_a[11]), .out(shifted_rs[13]), .sel(y_n));
  Multiplexer #(.enable("false")) multiplexer_15 (.in0(rs_a[14]), .in1(rs_a[12]), .out(shifted_rs[14]), .sel(y_n));
  Multiplexer #(.enable("false")) multiplexer_16 (.in0(rs_a[15]), .in1(rs_a[13]), .out(shifted_rs[15]), .sel(y_n));
endmodule

module bit_shofter_left_4 (
  input  in_1,
  input  [15:0] rs_a,
  input  y_n,
  output [15:0] shifted_rs
);

  Multiplexer #(.enable("false")) multiplexer_1 (.in0(rs_a[0]), .in1(in_1), .out(shifted_rs[0]), .sel(y_n));
  Multiplexer #(.enable("false")) multiplexer_2 (.in0(rs_a[1]), .in1(in_1), .out(shifted_rs[1]), .sel(y_n));
  Multiplexer #(.enable("false")) multiplexer_3 (.in0(rs_a[2]), .in1(in_1), .out(shifted_rs[2]), .sel(y_n));
  Multiplexer #(.enable("false")) multiplexer_4 (.in0(rs_a[3]), .in1(in_1), .out(shifted_rs[3]), .sel(y_n));
  Multiplexer #(.enable("false")) multiplexer_5 (.in0(rs_a[4]), .in1(rs_a[0]), .out(shifted_rs[4]), .sel(y_n));
  Multiplexer #(.enable("false")) multiplexer_6 (.in0(rs_a[5]), .in1(rs_a[1]), .out(shifted_rs[5]), .sel(y_n));
  Multiplexer #(.enable("false")) multiplexer_7 (.in0(rs_a[6]), .in1(rs_a[2]), .out(shifted_rs[6]), .sel(y_n));
  Multiplexer #(.enable("false")) multiplexer_8 (.in0(rs_a[7]), .in1(rs_a[3]), .out(shifted_rs[7]), .sel(y_n));
  Multiplexer #(.enable("false")) multiplexer_9 (.in0(rs_a[8]), .in1(rs_a[4]), .out(shifted_rs[8]), .sel(y_n));
  Multiplexer #(.enable("false")) multiplexer_10 (.in0(rs_a[9]), .in1(rs_a[5]), .out(shifted_rs[9]), .sel(y_n));
  Multiplexer #(.enable("false")) multiplexer_11 (.in0(rs_a[10]), .in1(rs_a[6]), .out(shifted_rs[10]), .sel(y_n));
  Multiplexer #(.enable("false")) multiplexer_12 (.in0(rs_a[11]), .in1(rs_a[7]), .out(shifted_rs[11]), .sel(y_n));
  Multiplexer #(.enable("false")) multiplexer_13 (.in0(rs_a[12]), .in1(rs_a[8]), .out(shifted_rs[12]), .sel(y_n));
  Multiplexer #(.enable("false")) multiplexer_14 (.in0(rs_a[13]), .in1(rs_a[9]), .out(shifted_rs[13]), .sel(y_n));
  Multiplexer #(.enable("false")) multiplexer_15 (.in0(rs_a[14]), .in1(rs_a[10]), .out(shifted_rs[14]), .sel(y_n));
  Multiplexer #(.enable("false")) multiplexer_16 (.in0(rs_a[15]), .in1(rs_a[11]), .out(shifted_rs[15]), .sel(y_n));
endmodule

module barrel_shifter_left (
  input  [15:0] rs_in,
  input  [2:0] bitshift,
  output [15:0] rs_out
);

  wire [15:0] bit_shift_left_2_1_shifted_rs, bit_shifter_left_1_shifted_rs;

  bit_shifter_left bit_shifter_left_1 (
    .rs_a(rs_in), .y_n(bitshift[0]), .shifted_rs(bit_shifter_left_1_shifted_rs));  // open: in_1
  bit_shift_left_2 bit_shift_left_2_1 (
    .rs_a(bit_shifter_left_1_shifted_rs), .y_n(bitshift[1]), .shifted_rs(bit_shift_left_2_1_shifted_rs));  // open: in_1
  bit_shofter_left_4 bit_shofter_left_4_1 (
    .rs_a(bit_shift_left_2_1_shifted_rs), .y_n(bitshift[2]), .shifted_rs(rs_out));  // open: in_1
endmodule

module arithmetic_shift (
  input  [15:0] in_1,
  input  [2:0] in_2,
  output [15:0] out_3
);

  wire [15:0] rshift_1_1_shifted_rs, rshift_2_1_shifted_rs;

  rshift_1 rshift_1_1 (.rs_a(in_1), .y_n(in_2[0]), .shifted_rs(rshift_1_1_shifted_rs));
  rshift_2 rshift_2_1 (.rs_a(rshift_1_1_shifted_rs), .y_n(in_2[1]), .shifted_rs(rshift_2_1_shifted_rs));
  rshift_4 rshift_4_1 (.rs_a(rshift_2_1_shifted_rs), .y_n(in_2[2]), .shifted_rs(out_3));
endmodule

module rshift_1 (
  input  [15:0] rs_a,
  input  y_n,
  output [15:0] shifted_rs
);

  Multiplexer #(.enable("false")) multiplexer_1 (.in0(rs_a[0]), .in1(rs_a[1]), .out(shifted_rs[0]), .sel(y_n));
  Multiplexer #(.enable("false")) multiplexer_2 (.in0(rs_a[1]), .in1(rs_a[2]), .out(shifted_rs[1]), .sel(y_n));
  Multiplexer #(.enable("false")) multiplexer_3 (.in0(rs_a[2]), .in1(rs_a[3]), .out(shifted_rs[2]), .sel(y_n));
  Multiplexer #(.enable("false")) multiplexer_4 (.in0(rs_a[3]), .in1(rs_a[4]), .out(shifted_rs[3]), .sel(y_n));
  Multiplexer #(.enable("false")) multiplexer_5 (.in0(rs_a[4]), .in1(rs_a[5]), .out(shifted_rs[4]), .sel(y_n));
  Multiplexer #(.enable("false")) multiplexer_6 (.in0(rs_a[5]), .in1(rs_a[6]), .out(shifted_rs[5]), .sel(y_n));
  Multiplexer #(.enable("false")) multiplexer_7 (.in0(rs_a[6]), .in1(rs_a[7]), .out(shifted_rs[6]), .sel(y_n));
  Multiplexer #(.enable("false")) multiplexer_8 (.in0(rs_a[7]), .in1(rs_a[8]), .out(shifted_rs[7]), .sel(y_n));
  Multiplexer #(.enable("false")) multiplexer_9 (.in0(rs_a[8]), .in1(rs_a[9]), .out(shifted_rs[8]), .sel(y_n));
  Multiplexer #(.enable("false")) multiplexer_10 (.in0(rs_a[9]), .in1(rs_a[10]), .out(shifted_rs[9]), .sel(y_n));
  Multiplexer #(.enable("false")) multiplexer_11 (.in0(rs_a[10]), .in1(rs_a[11]), .out(shifted_rs[10]), .sel(y_n));
  Multiplexer #(.enable("false")) multiplexer_12 (.in0(rs_a[11]), .in1(rs_a[12]), .out(shifted_rs[11]), .sel(y_n));
  Multiplexer #(.enable("false")) multiplexer_13 (.in0(rs_a[12]), .in1(rs_a[13]), .out(shifted_rs[12]), .sel(y_n));
  Multiplexer #(.enable("false")) multiplexer_14 (.in0(rs_a[13]), .in1(rs_a[14]), .out(shifted_rs[13]), .sel(y_n));
  Multiplexer #(.enable("false")) multiplexer_15 (.in0(rs_a[14]), .in1(rs_a[15]), .out(shifted_rs[14]), .sel(y_n));
  Multiplexer #(.enable("false")) multiplexer_16 (.in0(rs_a[15]), .in1(rs_a[15]), .out(shifted_rs[15]), .sel(y_n));
endmodule

module rshift_2 (
  input  [15:0] rs_a,
  input  y_n,
  output [15:0] shifted_rs
);

  Multiplexer #(.enable("false")) multiplexer_1 (.in0(rs_a[0]), .in1(rs_a[2]), .out(shifted_rs[0]), .sel(y_n));
  Multiplexer #(.enable("false")) multiplexer_2 (.in0(rs_a[1]), .in1(rs_a[3]), .out(shifted_rs[1]), .sel(y_n));
  Multiplexer #(.enable("false")) multiplexer_3 (.in0(rs_a[2]), .in1(rs_a[4]), .out(shifted_rs[2]), .sel(y_n));
  Multiplexer #(.enable("false")) multiplexer_4 (.in0(rs_a[3]), .in1(rs_a[5]), .out(shifted_rs[3]), .sel(y_n));
  Multiplexer #(.enable("false")) multiplexer_5 (.in0(rs_a[4]), .in1(rs_a[6]), .out(shifted_rs[4]), .sel(y_n));
  Multiplexer #(.enable("false")) multiplexer_6 (.in0(rs_a[5]), .in1(rs_a[7]), .out(shifted_rs[5]), .sel(y_n));
  Multiplexer #(.enable("false")) multiplexer_7 (.in0(rs_a[6]), .in1(rs_a[8]), .out(shifted_rs[6]), .sel(y_n));
  Multiplexer #(.enable("false")) multiplexer_8 (.in0(rs_a[7]), .in1(rs_a[9]), .out(shifted_rs[7]), .sel(y_n));
  Multiplexer #(.enable("false")) multiplexer_9 (.in0(rs_a[8]), .in1(rs_a[10]), .out(shifted_rs[8]), .sel(y_n));
  Multiplexer #(.enable("false")) multiplexer_10 (.in0(rs_a[9]), .in1(rs_a[11]), .out(shifted_rs[9]), .sel(y_n));
  Multiplexer #(.enable("false")) multiplexer_11 (.in0(rs_a[10]), .in1(rs_a[12]), .out(shifted_rs[10]), .sel(y_n));
  Multiplexer #(.enable("false")) multiplexer_12 (.in0(rs_a[11]), .in1(rs_a[13]), .out(shifted_rs[11]), .sel(y_n));
  Multiplexer #(.enable("false")) multiplexer_13 (.in0(rs_a[12]), .in1(rs_a[14]), .out(shifted_rs[12]), .sel(y_n));
  Multiplexer #(.enable("false")) multiplexer_14 (.in0(rs_a[13]), .in1(rs_a[15]), .out(shifted_rs[13]), .sel(y_n));
  Multiplexer #(.enable("false")) multiplexer_15 (.in0(rs_a[14]), .in1(rs_a[15]), .out(shifted_rs[14]), .sel(y_n));
  Multiplexer #(.enable("false")) multiplexer_16 (.in0(rs_a[15]), .in1(rs_a[15]), .out(shifted_rs[15]), .sel(y_n));
endmodule

module rshift_4 (
  input  [15:0] rs_a,
  input  y_n,
  output [15:0] shifted_rs
);

  Multiplexer #(.enable("false")) multiplexer_1 (.in0(rs_a[0]), .in1(rs_a[4]), .out(shifted_rs[0]), .sel(y_n));
  Multiplexer #(.enable("false")) multiplexer_2 (.in0(rs_a[2]), .in1(rs_a[6]), .out(shifted_rs[2]), .sel(y_n));
  Multiplexer #(.enable("false")) multiplexer_3 (.in0(rs_a[3]), .in1(rs_a[7]), .out(shifted_rs[3]), .sel(y_n));
  Multiplexer #(.enable("false")) multiplexer_4 (.in0(rs_a[4]), .in1(rs_a[8]), .out(shifted_rs[4]), .sel(y_n));
  Multiplexer #(.enable("false")) multiplexer_5 (.in0(rs_a[5]), .in1(rs_a[9]), .out(shifted_rs[5]), .sel(y_n));
  Multiplexer #(.enable("false")) multiplexer_6 (.in0(rs_a[6]), .in1(rs_a[10]), .out(shifted_rs[6]), .sel(y_n));
  Multiplexer #(.enable("false")) multiplexer_7 (.in0(rs_a[7]), .in1(rs_a[11]), .out(shifted_rs[7]), .sel(y_n));
  Multiplexer #(.enable("false")) multiplexer_8 (.in0(rs_a[8]), .in1(rs_a[12]), .out(shifted_rs[8]), .sel(y_n));
  Multiplexer #(.enable("false")) multiplexer_9 (.in0(rs_a[9]), .in1(rs_a[13]), .out(shifted_rs[9]), .sel(y_n));
  Multiplexer #(.enable("false")) multiplexer_10 (.in0(rs_a[10]), .in1(rs_a[14]), .out(shifted_rs[10]), .sel(y_n));
  Multiplexer #(.enable("false")) multiplexer_11 (.in0(rs_a[11]), .in1(rs_a[15]), .out(shifted_rs[11]), .sel(y_n));
  Multiplexer #(.enable("false")) multiplexer_12 (.in0(rs_a[12]), .in1(rs_a[15]), .out(shifted_rs[12]), .sel(y_n));
  Multiplexer #(.enable("false")) multiplexer_13 (.in0(rs_a[13]), .in1(rs_a[15]), .out(shifted_rs[13]), .sel(y_n));
  Multiplexer #(.enable("false")) multiplexer_14 (.in0(rs_a[14]), .in1(rs_a[15]), .out(shifted_rs[14]), .sel(y_n));
  Multiplexer #(.enable("false")) multiplexer_15 (.in0(rs_a[15]), .in1(rs_a[15]), .out(shifted_rs[15]), .sel(y_n));
  Multiplexer #(.enable("false")) multiplexer_16 (.in0(rs_a[1]), .in1(rs_a[5]), .out(shifted_rs[1]), .sel(y_n));
endmodule

module pc_mod (
  input  a,
  input  carryin,
  output out,
  output ovf
);

  xor xor_1 (out, a, carryin);
  and and_1 (ovf, a, carryin);
endmodule

module pc_counter (
  input  [15:0] pc,
  output [15:0] pcplus1
);

  wire pc_mod_1_ovf, pc_mod_2_ovf, pc_mod_3_ovf, pc_mod_4_ovf, pc_mod_5_ovf, pc_mod_6_ovf, pc_mod_7_ovf,
       pc_mod_8_ovf, pc_mod_9_ovf, pc_mod_10_ovf, pc_mod_13_ovf, pc_mod_14_ovf, pc_mod_15_ovf;

  pc_mod pc_mod_1 (.a(pc[0]), .carryin(1'b1), .out(pcplus1[0]), .ovf(pc_mod_1_ovf));
  pc_mod pc_mod_2 (.a(pc[8]), .carryin(pc_mod_15_ovf), .out(pcplus1[8]), .ovf(pc_mod_2_ovf));
  pc_mod pc_mod_3 (.a(pc[1]), .carryin(pc_mod_1_ovf), .out(pcplus1[1]), .ovf(pc_mod_3_ovf));
  pc_mod pc_mod_4 (.a(pc[2]), .carryin(pc_mod_3_ovf), .out(pcplus1[2]), .ovf(pc_mod_4_ovf));
  pc_mod pc_mod_5 (.a(pc[9]), .carryin(pc_mod_2_ovf), .out(pcplus1[9]), .ovf(pc_mod_5_ovf));
  pc_mod pc_mod_6 (.a(pc[10]), .carryin(pc_mod_5_ovf), .out(pcplus1[10]), .ovf(pc_mod_6_ovf));
  pc_mod pc_mod_7 (.a(pc[3]), .carryin(pc_mod_4_ovf), .out(pcplus1[3]), .ovf(pc_mod_7_ovf));
  pc_mod pc_mod_8 (.a(pc[4]), .carryin(pc_mod_7_ovf), .out(pcplus1[4]), .ovf(pc_mod_8_ovf));
  pc_mod pc_mod_9 (.a(pc[11]), .carryin(pc_mod_6_ovf), .out(pcplus1[11]), .ovf(pc_mod_9_ovf));
  pc_mod pc_mod_10 (.a(pc[12]), .carryin(pc_mod_9_ovf), .out(pcplus1[12]), .ovf(pc_mod_10_ovf));
  pc_mod pc_mod_11 (.a(pc[5]), .carryin(pc_mod_8_ovf), .out(pcplus1[5]));  // open: ovf
  pc_mod pc_mod_12 (.a(pc[6]), .out(pcplus1[6]));  // open: carryin, ovf
  pc_mod pc_mod_13 (.a(pc[13]), .carryin(pc_mod_10_ovf), .out(pcplus1[13]), .ovf(pc_mod_13_ovf));
  pc_mod pc_mod_14 (.a(pc[14]), .carryin(pc_mod_13_ovf), .out(pcplus1[14]), .ovf(pc_mod_14_ovf));
  pc_mod pc_mod_15 (.a(pc[7]), .out(pcplus1[7]), .ovf(pc_mod_15_ovf));  // open: carryin
  pc_mod pc_mod_16 (.a(pc[15]), .carryin(pc_mod_14_ovf), .out(pcplus1[15]));  // open: ovf
endmodule

module combinatorial_logic (
  input  [15:0] in_1,
  output [2:0] rs,
  output [2:0] rt,
  output [2:0] rd,
  output [2:0] shamt,
  output [5:0] immed,
  output [11:0] address,
  output is_beq,
  output MUX_j_vs_pc,
  output is_bgt,
  output is_output,
  output load_mem_to_input,
  output is_addi,
  output write_enable_RAM,
  output MUX_data_vs_rs,
  output is_input,
  output is_jal,
  output sei_or_rt,
  output [2:0] alu1_chooser,
  output [1:0] PC_ctrl,
  output not_sw
);

  wire decoder_1_out2, decoder_1_out3, decoder_1_out6, decoder_1_out7, decoder_1_out8, decoder_1_out9,
       decoder_1_out10, decoder_1_out11, decoder_1_out12, decoder_1_out13, decoder_1_out14, or_9_out;

  Decoder #(.select(4)) decoder_1 (
    .out0(is_output), .out1(is_input), .out2(decoder_1_out2), .out3(decoder_1_out3), .out4(is_beq),
    .out5(is_bgt), .out6(decoder_1_out6), .out7(decoder_1_out7), .out8(decoder_1_out8),
    .out9(decoder_1_out9), .out10(decoder_1_out10), .out11(decoder_1_out11), .out12(decoder_1_out12),
    .out13(decoder_1_out13), .out14(decoder_1_out14), .out15(is_jal), .sel(in_1[15:12]));  // open: en
  or or_1 (sei_or_rt, decoder_1_out2, decoder_1_out3, decoder_1_out8);
  or or_2 (is_addi, decoder_1_out8, decoder_1_out2, decoder_1_out3);
  or or_3 (alu1_chooser[2], decoder_1_out11, decoder_1_out6);
  or or_4 (PC_ctrl[0], decoder_1_out14, decoder_1_out13);
  or or_5 (alu1_chooser[1], decoder_1_out7, decoder_1_out12);
  or or_6 (alu1_chooser[0], is_beq, is_bgt, decoder_1_out12, decoder_1_out6, decoder_1_out10);
  buf or_7 (write_enable_RAM, decoder_1_out3);  // OR_Gate
  buf or_8 (load_mem_to_input, decoder_1_out2);  // OR_Gate
  or or_9 (or_9_out, is_jal, decoder_1_out3, is_beq, decoder_1_out13, is_bgt);
  not not_1 (not_sw, or_9_out);
  buf or_10 (MUX_data_vs_rs, decoder_1_out2);  // OR_Gate
  or or_11 (MUX_j_vs_pc, is_jal, decoder_1_out14, decoder_1_out13);

  assign address = in_1[11:0];
  assign immed = in_1[5:0];
  assign PC_ctrl[1] = is_jal;
  assign rd = in_1[5:3];
  assign rs = in_1[11:9];
  assign rt = in_1[8:6];
  assign shamt = in_1[2:0];

  // Other names for the same wires on the sheet: input_print = is_input; print_rs = is_output

  // Notes on the sheet:
  //   control command factoring
  //   rs
  //   rt
  //   address
  //   rd
  //   shamt
  //   immediate
endmodule

module TTY_wrapper (
  input  [15:0] in_1,
  output [6:0] out_2
);


  assign out_2 = in_1[6:0];
endmodule

module keyboard_wrapper (
  input  [6:0] in_1,
  input  is_valid,
  output [15:0] out_3
);

  not not_1 (out_3[7], is_valid);
  not not_2 (out_3[15], 1'b1);

  assign {out_3[14:8], out_3[6:0]} = {{7{out_3[15]}}, in_1};
endmodule

module pc_extender (
  input  [11:0] in_1,
  input  [15:0] in_2,
  output [15:0] L
);


  assign L = {in_2[15:12], in_1};
endmodule
